# Fritzing sketch VeeraGudla and RonOmbaoCENG317RCCarDiagram (Final PCB) (saved by Fritzing 0.9.4)
circuit board: 15.0428cm x 9.285cm
breadboards: 1

parts:
  BackWheel1 = DC Motor
  FrontWheel2 = DC Motor
  FrontWheel1 = DC Motor
  BackWheel2 = DC Motor
  L293Vcc = Battery block 9V
  IC1 = L293D [package=THT]
  SensPoteniometer = POT [package=3362u]
  R3 = Resistor [tolerance=±5% resistance=220 package=THT]
  R1 = Resistor [tolerance=±5% resistance=220 package=THT]
  IREmitter = LED - 3mm [color="Infrared (850nm)" package="3 mm [THT]"]
  IRPhotodiode = LED - 3mm [color="Infrared (940nm)" package="3 mm [THT]"]
  DetectLED = LED - 3mm [color="Red (633nm)" package="3 mm [THT]"]
  SteeringServo = Dagu DGServo 9g (Pan and tilt) [part_number=RS001B]
  R2 = Resistor [tolerance=±5% resistance=10k package=THT]
  Raspberry_Pi3 = Raspberry Pi 3 [part_number=RPI-3-V1.2]
  JP1 = Header 6 [package=molex-1x6_lock]
  Q1 = TRANSISTOR_NPN [package=to-92]
  Buzzer = Buzzer 12mm [package=buzzer-12mm-ns-kit]
  R4 = Resistor [tolerance=±5% resistance=220 package=THT]
  R5 = Resistor [tolerance=±5% resistance=220 package=THT]
  LED1 = LED - 3mm [color="Red (633nm)" package="3 mm [THT]"]
  U1 = LM 358 Dual Op-Amp [package="DIP8 [THT]"]

nets:
  N1: BackWheel1.pin_1, BackWheel2.pin_1, IC1.Out_1_(_Controlled_by_Enable_1_)
  N2: BackWheel1.pin_2, BackWheel2.pin_2, IC1.Out_2_(_Controlled_by_Enable_1_)
  N3: FrontWheel2.pin_1, FrontWheel1.pin_1, IC1.Out_4_(_Controlled_by_Enable_2_)
  N4: FrontWheel2.pin_2, FrontWheel1.pin_2, IC1.Out_3_(_Controlled_by_Enable_2_)
  9V/GND: L293Vcc.-, L293Vcc.+, IC1.0V, IC1.+Vmotor, IC1.+V, SensPoteniometer.A, R3.Pin_0, R1.Pin_0, SteeringServo.gnd, R2.Pin_0, Raspberry_Pi3.GND, Raspberry_Pi3.GIPO26, JP1.2, Q1.E, Buzzer.2, U1.connector3
  ToGPIO25: IC1.Enable_1, Raspberry_Pi3.GIPO25
  ToGPIO24: IC1.In_1, Raspberry_Pi3.GIPO24
  ToGPIO23: IC1.In_2, Raspberry_Pi3.GIPO23
  ToGPIO17: IC1.Enable_2, Raspberry_Pi3.GIPO17
  ToGPIO27: IC1.In_3, Raspberry_Pi3.GIPO27
  ToGPIO22: IC1.In_4, Raspberry_Pi3.GIPO22
  3V3: SensPoteniometer.E, IREmitter.anode, IRPhotodiode.cathode, IRPhotodiode.anode, R2.Pin_1, Raspberry_Pi3.3v3, Raspberry_Pi3.3V3, U1.connector1, U1.connector7
  N5: SensPoteniometer.S, U1.connector2
  N6: R3.Pin_1, DetectLED.cathode
  N7: R1.Pin_1, IREmitter.cathode
  GPIO26: DetectLED.anode, U1.connector0
  VCC: SteeringServo.vcc, Raspberry_Pi3.5V
  ToGPIO5: SteeringServo.pulse, Raspberry_Pi3.GIPO5
  SDA_3V3: Raspberry_Pi3.GPIO2, JP1.4
  SCL_3V3: Raspberry_Pi3.GPIO3, JP1.3
  ToGPIO21: Raspberry_Pi3.GIPO21, R5.Pin_0
  N8: Raspberry_Pi3.GIPO16, Buzzer.1
  3.3V: JP1.1, R4.Pin_1
  N9: Q1.B, R5.Pin_1
  N10: Q1.C, LED1.cathode
  N11: R4.Pin_0, LED1.anode

notes:
  II. RC CAR MAIN COMPONENT
  I. SENSOR
